// Logisim project PC.circ as structural Verilog: 31 circuits, main circuit main
module main (
  input  [3:0] in_1,
  input  [3:0] in_2,
  output [3:0] out_3
);

  Subtractor #(.width(4)) subtractor_1 (.a(in_1), .b(in_2), .out(out_3));  // open: bin, bout
endmodule

module CAnd (
  input  in_1,
  input  in_2,
  output out_3
);

  wire nand_1_out;

  nand nand_1 (nand_1_out, in_1, in_2);
  nand nand_2 (out_3, nand_1_out, nand_1_out);
endmodule

module COR (
  input  in_1,
  input  in_2,
  output out_3
);

  wire nand_1_out, nand_2_out;

  nand nand_1 (nand_1_out, in_1, in_1);
  nand nand_2 (nand_2_out, in_2, in_2);
  nand nand_3 (out_3, nand_1_out, nand_2_out);
endmodule

module CNOT (
  input  in_1,
  output out_2
);

  nand nand_1 (out_2, in_1, in_1);
endmodule

module CXOR (
  input  in_1,
  input  in_2,
  output out_3
);

  wire nand_1_out, nand_2_out, nand_3_out;

  nand nand_1 (nand_1_out, in_1, in_2);
  nand nand_2 (nand_2_out, in_1, nand_1_out);
  nand nand_3 (nand_3_out, nand_1_out, in_2);
  nand nand_4 (out_3, nand_2_out, nand_3_out);
endmodule

module CMUX (
  input  in_1,
  input  in_2,
  input  in_3,
  output out_4
);

  wire and_1_out, xor_1_out;

  xor xor_1 (xor_1_out, in_1, in_3);
  and and_1 (and_1_out, in_2, in_3);
  or or_1 (out_4, xor_1_out, and_1_out);
endmodule

module CDMUX (
  input  in_1,
  input  in_2,
  output out_3,
  output out_4
);

  wire not_1_out;

  and and_1 (out_3, in_1, in_2);
  and and_2 (out_4, in_1, not_1_out);
  not not_1 (not_1_out, in_2);
endmodule

module MUX4WAY16 (
  input  [15:0] A,
  input  [15:0] B,
  input  [15:0] C,
  input  [15:0] D,
  input  [1:0] in_5,
  output [15:0] out_6
);

  wire not_1_out, splitter2_1_out_2, splitter2_1_out_3;
  wire [15:0] mux16_1_o, mux16_2_o, mux16_3_o, mux16_4_o, mux16_5_o, mux16_6_o;

  MUX16 mux16_1 (.S(not_1_out), .A(A), .O(mux16_1_o));  // open: B
  MUX16 mux16_2 (.S(not_1_out), .A(B), .O(mux16_2_o));  // open: B
  MUX16 mux16_3 (.S(not_1_out), .B(C), .O(mux16_3_o));  // open: A
  MUX16 mux16_4 (.S(not_1_out), .B(D), .O(mux16_4_o));  // open: A
  not not_1 (not_1_out, splitter2_1_out_2);
  SPLITTER2 splitter2_1 (.in_1(in_5), .out_3(splitter2_1_out_3), .out_2(splitter2_1_out_2));
  MUX16 mux16_5 (.S(splitter2_1_out_3), .A(mux16_2_o), .B(mux16_1_o), .O(mux16_5_o));
  MUX16 mux16_6 (.S(splitter2_1_out_3), .A(mux16_4_o), .B(mux16_3_o), .O(mux16_6_o));
  assign out_6 = mux16_5_o | mux16_6_o;  // OR_Gate or_1, 16 bits wide
endmodule

module MUX16 (
  input  S,
  input  [15:0] A,
  input  [15:0] B,
  output [15:0] O
);

  wire and_1_out, and_2_out, and_3_out, and_4_out, and_5_out, and_6_out, and_7_out, and_8_out, and_9_out,
       and_10_out, and_11_out, and_12_out, and_13_out, and_14_out, and_15_out, and_16_out, and_17_out,
       and_18_out, and_19_out, and_20_out, and_21_out, and_22_out, and_23_out, and_24_out, and_25_out,
       and_26_out, and_27_out, and_28_out, and_29_out, and_30_out, and_31_out, and_32_out, not_1_out,
       splitter16_1_out_2, splitter16_1_out_3, splitter16_1_out_4, splitter16_1_out_5, splitter16_1_out_6,
       splitter16_1_out_7, splitter16_1_out_8, splitter16_1_out_9, splitter16_1_out_10, splitter16_1_out_11,
       splitter16_1_out_12, splitter16_1_out_13, splitter16_1_out_14, splitter16_1_out_15,
       splitter16_1_out_16, splitter16_1_out_17, splitter16_2_out_2, splitter16_2_out_3, splitter16_2_out_4,
       splitter16_2_out_5, splitter16_2_out_6, splitter16_2_out_7, splitter16_2_out_8, splitter16_2_out_9,
       splitter16_2_out_10, splitter16_2_out_11, splitter16_2_out_12, splitter16_2_out_13,
       splitter16_2_out_14, splitter16_2_out_15, splitter16_2_out_16, splitter16_2_out_17;
  wire [15:0] merger16_1_out_17, merger16_2_out_17;

  Splitter16 splitter16_1 (
    .in_1(A), .out_3(splitter16_1_out_3), .out_4(splitter16_1_out_4), .out_5(splitter16_1_out_5),
    .out_6(splitter16_1_out_6), .out_7(splitter16_1_out_7), .out_8(splitter16_1_out_8),
    .out_9(splitter16_1_out_9), .out_10(splitter16_1_out_10), .out_11(splitter16_1_out_11),
    .out_12(splitter16_1_out_12), .out_13(splitter16_1_out_13), .out_14(splitter16_1_out_14),
    .out_15(splitter16_1_out_15), .out_16(splitter16_1_out_16), .out_17(splitter16_1_out_17),
    .out_2(splitter16_1_out_2));
  Splitter16 splitter16_2 (
    .in_1(B), .out_3(splitter16_2_out_3), .out_4(splitter16_2_out_4), .out_5(splitter16_2_out_5),
    .out_6(splitter16_2_out_6), .out_7(splitter16_2_out_7), .out_8(splitter16_2_out_8),
    .out_9(splitter16_2_out_9), .out_10(splitter16_2_out_10), .out_11(splitter16_2_out_11),
    .out_12(splitter16_2_out_12), .out_13(splitter16_2_out_13), .out_14(splitter16_2_out_14),
    .out_15(splitter16_2_out_15), .out_16(splitter16_2_out_16), .out_17(splitter16_2_out_17),
    .out_2(splitter16_2_out_2));
  not not_1 (not_1_out, S);
  and and_1 (and_1_out, S, splitter16_1_out_2);
  and and_2 (and_2_out, S, splitter16_1_out_3);
  and and_3 (and_3_out, S, splitter16_1_out_4);
  and and_4 (and_4_out, S, splitter16_1_out_5);
  and and_5 (and_5_out, S, splitter16_1_out_6);
  and and_6 (and_6_out, S, splitter16_1_out_7);
  and and_7 (and_7_out, S, splitter16_1_out_8);
  and and_8 (and_8_out, S, splitter16_1_out_9);
  and and_9 (and_9_out, S, splitter16_1_out_10);
  and and_10 (and_10_out, S, splitter16_1_out_11);
  and and_11 (and_11_out, S, splitter16_1_out_12);
  and and_12 (and_12_out, S, splitter16_1_out_13);
  and and_13 (and_13_out, S, splitter16_1_out_14);
  and and_14 (and_14_out, S, splitter16_1_out_15);
  and and_15 (and_15_out, S, splitter16_1_out_16);
  and and_16 (and_16_out, S, splitter16_1_out_17);
  and and_17 (and_17_out, not_1_out, splitter16_2_out_2);
  and and_18 (and_18_out, not_1_out, splitter16_2_out_3);
  and and_19 (and_19_out, not_1_out, splitter16_2_out_4);
  and and_20 (and_20_out, not_1_out, splitter16_2_out_5);
  and and_21 (and_21_out, not_1_out, splitter16_2_out_6);
  and and_22 (and_22_out, not_1_out, splitter16_2_out_7);
  and and_23 (and_23_out, not_1_out, splitter16_2_out_8);
  and and_24 (and_24_out, not_1_out, splitter16_2_out_9);
  and and_25 (and_25_out, not_1_out, splitter16_2_out_10);
  and and_26 (and_26_out, not_1_out, splitter16_2_out_11);
  and and_27 (and_27_out, not_1_out, splitter16_2_out_12);
  and and_28 (and_28_out, not_1_out, splitter16_2_out_13);
  and and_29 (and_29_out, not_1_out, splitter16_2_out_14);
  and and_30 (and_30_out, not_1_out, splitter16_2_out_15);
  and and_31 (and_31_out, not_1_out, splitter16_2_out_16);
  and and_32 (and_32_out, not_1_out, splitter16_2_out_17);
  Merger16 merger16_1 (
    .in_2(and_2_out), .in_3(and_3_out), .in_4(and_4_out), .in_5(and_5_out), .in_6(and_6_out),
    .in_7(and_7_out), .in_8(and_8_out), .in_9(and_9_out), .in_10(and_10_out), .in_11(and_11_out),
    .in_1(and_1_out), .in_12(and_12_out), .in_13(and_13_out), .in_14(and_14_out), .in_15(and_15_out),
    .in_16(and_16_out), .out_17(merger16_1_out_17));
  Merger16 merger16_2 (
    .in_2(and_18_out), .in_3(and_19_out), .in_4(and_20_out), .in_5(and_21_out), .in_6(and_22_out),
    .in_7(and_23_out), .in_8(and_24_out), .in_9(and_25_out), .in_10(and_26_out), .in_11(and_27_out),
    .in_1(and_17_out), .in_12(and_28_out), .in_13(and_29_out), .in_14(and_30_out), .in_15(and_31_out),
    .in_16(and_32_out), .out_17(merger16_2_out_17));
  assign O = merger16_1_out_17 ^ merger16_2_out_17;  // XOR_Gate xor_1, 16 bits wide
endmodule

module AND16 (
  input  [15:0] A,
  input  [15:0] B,
  output [15:0] out_3
);

  wire and_1_out, and_3_out, and_4_out, and_5_out, and_6_out, and_11_out, and_12_out, and_13_out,
       splitter16_1_out_2, splitter16_1_out_3, splitter16_1_out_4, splitter16_1_out_5, splitter16_1_out_6,
       splitter16_1_out_7, splitter16_1_out_8, splitter16_1_out_9, splitter16_1_out_10, splitter16_1_out_11,
       splitter16_1_out_12, splitter16_1_out_13, splitter16_1_out_14, splitter16_1_out_15,
       splitter16_1_out_16, splitter16_1_out_17, splitter16_2_out_2, splitter16_2_out_3, splitter16_2_out_4,
       splitter16_2_out_5, splitter16_2_out_6, splitter16_2_out_7, splitter16_2_out_8, splitter16_2_out_9,
       splitter16_2_out_10, splitter16_2_out_11, splitter16_2_out_12, splitter16_2_out_13,
       splitter16_2_out_14, splitter16_2_out_15, splitter16_2_out_16, splitter16_2_out_17;

  Splitter16 splitter16_1 (
    .in_1(A), .out_3(splitter16_1_out_3), .out_4(splitter16_1_out_4), .out_5(splitter16_1_out_5),
    .out_6(splitter16_1_out_6), .out_7(splitter16_1_out_7), .out_8(splitter16_1_out_8),
    .out_9(splitter16_1_out_9), .out_10(splitter16_1_out_10), .out_11(splitter16_1_out_11),
    .out_12(splitter16_1_out_12), .out_13(splitter16_1_out_13), .out_14(splitter16_1_out_14),
    .out_15(splitter16_1_out_15), .out_16(splitter16_1_out_16), .out_17(splitter16_1_out_17),
    .out_2(splitter16_1_out_2));
  Splitter16 splitter16_2 (
    .in_1(B), .out_3(splitter16_2_out_3), .out_4(splitter16_2_out_4), .out_5(splitter16_2_out_5),
    .out_6(splitter16_2_out_6), .out_7(splitter16_2_out_7), .out_8(splitter16_2_out_8),
    .out_9(splitter16_2_out_9), .out_10(splitter16_2_out_10), .out_11(splitter16_2_out_11),
    .out_12(splitter16_2_out_12), .out_13(splitter16_2_out_13), .out_14(splitter16_2_out_14),
    .out_15(splitter16_2_out_15), .out_16(splitter16_2_out_16), .out_17(splitter16_2_out_17),
    .out_2(splitter16_2_out_2));
  and and_1 (and_1_out, splitter16_1_out_2, splitter16_2_out_2);
  // AND_Gate and_2 has open pins: in0=splitter16_1_out_10, in1=splitter16_2_out_10, out=open
  and and_3 (and_3_out, splitter16_1_out_3, splitter16_2_out_3);
  and and_4 (and_4_out, splitter16_1_out_4, splitter16_2_out_4);
  and and_5 (and_5_out, splitter16_1_out_5, splitter16_2_out_5);
  and and_6 (and_6_out, splitter16_1_out_6, splitter16_2_out_6);
  // AND_Gate and_7 has open pins: in0=splitter16_1_out_11, in1=splitter16_2_out_11, out=open
  // AND_Gate and_8 has open pins: in0=splitter16_1_out_12, in1=splitter16_2_out_12, out=open
  // AND_Gate and_9 has open pins: in0=splitter16_1_out_13, in1=splitter16_2_out_13, out=open
  // AND_Gate and_10 has open pins: in0=splitter16_1_out_14, in1=splitter16_2_out_14, out=open
  and and_11 (and_11_out, splitter16_1_out_7, splitter16_2_out_7);
  and and_12 (and_12_out, splitter16_1_out_8, splitter16_2_out_8);
  and and_13 (and_13_out, splitter16_1_out_9, splitter16_2_out_9);
  // AND_Gate and_14 has open pins: in0=splitter16_1_out_15, in1=splitter16_2_out_15, out=open
  // AND_Gate and_15 has open pins: in0=splitter16_1_out_16, in1=splitter16_2_out_16, out=open
  // AND_Gate and_16 has open pins: in0=splitter16_1_out_17, in1=splitter16_2_out_17, out=open
  Merger16 merger16_1 (
    .in_2(and_3_out), .in_3(and_4_out), .in_4(and_5_out), .in_5(and_6_out), .in_6(and_11_out),
    .in_7(and_12_out), .in_8(and_13_out), .in_1(and_1_out), .out_17(out_3));  // open: in_9, in_10, in_11, in_12, in_13, in_14, in_15, in_16
endmodule

module Splitter16 (
  input  [15:0] in_1,
  output out_2,
  output out_3,
  output out_4,
  output out_5,
  output out_6,
  output out_7,
  output out_8,
  output out_9,
  output out_10,
  output out_11,
  output out_12,
  output out_13,
  output out_14,
  output out_15,
  output out_16,
  output out_17
);

  BitSelector #(.width(16)) bitselector_1 (.in(in_1), .out(out_2), .sel(4'b0000));
  BitSelector #(.width(16)) bitselector_2 (.in(in_1), .out(out_3), .sel(4'b0001));
  BitSelector #(.width(16)) bitselector_3 (.in(in_1), .out(out_4), .sel(4'b0010));
  BitSelector #(.width(16)) bitselector_4 (.in(in_1), .out(out_5), .sel(4'b0011));
  BitSelector #(.width(16)) bitselector_5 (.in(in_1), .out(out_6), .sel(4'b0100));
  BitSelector #(.width(16)) bitselector_6 (.in(in_1), .out(out_7), .sel(4'b0101));
  BitSelector #(.width(16)) bitselector_7 (.in(in_1), .out(out_8), .sel(4'b0110));
  BitSelector #(.width(16)) bitselector_8 (.in(in_1), .out(out_9), .sel(4'b0111));
  BitSelector #(.width(16)) bitselector_9 (.in(in_1), .out(out_10), .sel(4'b1000));
  BitSelector #(.width(16)) bitselector_10 (.in(in_1), .out(out_11), .sel(4'b1001));
  BitSelector #(.width(16)) bitselector_11 (.in(in_1), .out(out_12), .sel(4'b1010));
  BitSelector #(.width(16)) bitselector_12 (.in(in_1), .out(out_13), .sel(4'b1011));
  BitSelector #(.width(16)) bitselector_13 (.in(in_1), .out(out_14), .sel(4'b1100));
  BitSelector #(.width(16)) bitselector_14 (.in(in_1), .out(out_15), .sel(4'b1101));
  BitSelector #(.width(16)) bitselector_15 (.in(in_1), .out(out_16), .sel(4'b1111));
  BitSelector #(.width(16)) bitselector_16 (.in(in_1), .out(out_17), .sel(4'b1111));
endmodule

module Splitter4 (
  input  [3:0] in_1,
  output out_2,
  output out_3,
  output out_4,
  output out_5
);

  BitSelector #(.width(4)) bitselector_1 (.in(in_1), .out(out_2), .sel(2'b00));
  BitSelector #(.width(4)) bitselector_2 (.in(in_1), .out(out_3), .sel(2'b01));
  BitSelector #(.width(4)) bitselector_3 (.in(in_1), .out(out_4), .sel(2'b10));
  BitSelector #(.width(4)) bitselector_4 (.in(in_1), .out(out_5), .sel(2'b11));
endmodule

module Merger16 (
  input  in_1,
  input  in_2,
  input  in_3,
  input  in_4,
  input  in_5,
  input  in_6,
  input  in_7,
  input  in_8,
  input  in_9,
  input  in_10,
  input  in_11,
  input  in_12,
  input  in_13,
  input  in_14,
  input  in_15,
  input  in_16,
  output [15:0] out_17
);

  wire [15:0] pla_1_out, pla_2_out, pla_3_out, pla_4_out, pla_5_out, pla_6_out, pla_7_out, pla_8_out,
       pla_9_out, pla_10_out, pla_11_out, pla_12_out, pla_13_out, pla_14_out, pla_15_out, pla_16_out;

  PLA #(.in_width(1), .out_width(16), .\table ("0 0000000000000000\n1 0000000000000001")) pla_1 (
    .in(in_1), .out(pla_1_out));
  PLA #(.in_width(1), .out_width(16), .\table ("0 0000000000000000\n1 0000000000000010")) pla_2 (
    .in(in_2), .out(pla_2_out));
  PLA #(.in_width(1), .out_width(16), .\table ("0 0000000000000000\n1 0000000000000100")) pla_3 (
    .in(in_3), .out(pla_3_out));
  PLA #(.in_width(1), .out_width(16), .\table ("0 0000000000000000\n1 0000000000001000")) pla_4 (
    .in(in_4), .out(pla_4_out));
  PLA #(.in_width(1), .out_width(16), .\table ("0 0000000000000000\n1 0000000000010000")) pla_5 (
    .in(in_5), .out(pla_5_out));
  PLA #(.in_width(1), .out_width(16), .\table ("0 0000000000000000\n1 0000000000100000")) pla_6 (
    .in(in_6), .out(pla_6_out));
  PLA #(.in_width(1), .out_width(16), .\table ("0 0000000000000000\n1 0000000001000000")) pla_7 (
    .in(in_7), .out(pla_7_out));
  PLA #(.in_width(1), .out_width(16), .\table ("0 0000000000000000\n1 0000000010000000")) pla_8 (
    .in(in_8), .out(pla_8_out));
  PLA #(.in_width(1), .out_width(16), .\table ("0 0000000000000000\n1 0000000100000000")) pla_9 (
    .in(in_9), .out(pla_9_out));
  PLA #(.in_width(1), .out_width(16), .\table ("0 0000000000000000\n1 0000001000000000")) pla_10 (
    .in(in_10), .out(pla_10_out));
  PLA #(.in_width(1), .out_width(16), .\table ("0 0000000000000000\n1 0000010000000000")) pla_11 (
    .in(in_11), .out(pla_11_out));
  PLA #(.in_width(1), .out_width(16), .\table ("0 0000000000000000\n1 0000100000000000")) pla_12 (
    .in(in_12), .out(pla_12_out));
  PLA #(.in_width(1), .out_width(16), .\table ("0 0000000000000000\n1 0001000000000000")) pla_13 (
    .in(in_13), .out(pla_13_out));
  PLA #(.in_width(1), .out_width(16), .\table ("0 0000000000000000\n1 0010000000000000")) pla_14 (
    .in(in_14), .out(pla_14_out));
  PLA #(.in_width(1), .out_width(16), .\table ("0 0000000000000000\n1 0100000000000000")) pla_15 (
    .in(in_15), .out(pla_15_out));
  PLA #(.in_width(1), .out_width(16), .\table ("0 0000000000000000\n1 1000000000000000")) pla_16 (
    .in(in_16), .out(pla_16_out));
  assign out_17 = pla_1_out | pla_2_out | pla_3_out | pla_4_out | pla_5_out | pla_6_out | pla_7_out | pla_8_out | pla_9_out | pla_10_out | pla_11_out | pla_12_out | pla_13_out | pla_14_out | pla_15_out | pla_16_out;  // OR_Gate or_1, 16 bits wide
endmodule

module Merger4 (
  input  in_1,
  input  in_2,
  input  in_3,
  input  in_4,
  output out_5
);

  or or_1 (out_5, in_4, in_3);
  // OR_Gate or_2 has open pins: in0=in_4, in1=in_2, out=open
endmodule

module SPLITTER2 (
  input  [1:0] in_1,
  output out_2,
  output out_3
);

  BitSelector #(.width(2)) bitselector_1 (.in(in_1), .out(out_2), .sel(1'b0));
  BitSelector #(.width(2)) bitselector_2 (.in(in_1), .out(out_3), .sel(1'b1));
endmodule

module DMUX16 (
  input  [15:0] in_1,
  input  in_2,
  output [15:0] out_3,
  output [15:0] out_4
);

  wire and_1_out, and_2_out, and_3_out, and_4_out, and_5_out, and_6_out, and_7_out, and_8_out, and_9_out,
       and_10_out, and_11_out, and_12_out, and_13_out, and_14_out, and_15_out, and_16_out, and_17_out,
       and_18_out, and_19_out, and_20_out, and_21_out, and_22_out, and_23_out, and_24_out, and_25_out,
       and_26_out, and_27_out, and_28_out, and_29_out, and_30_out, and_31_out, and_32_out, not_1_out,
       splitter16_1_out_2, splitter16_1_out_3, splitter16_1_out_4, splitter16_1_out_5, splitter16_1_out_6,
       splitter16_1_out_7, splitter16_1_out_8, splitter16_1_out_9, splitter16_1_out_10, splitter16_1_out_11,
       splitter16_1_out_12, splitter16_1_out_13, splitter16_1_out_14, splitter16_1_out_15,
       splitter16_1_out_16, splitter16_1_out_17;

  Splitter16 splitter16_1 (
    .in_1(in_1), .out_3(splitter16_1_out_3), .out_4(splitter16_1_out_4), .out_5(splitter16_1_out_5),
    .out_6(splitter16_1_out_6), .out_7(splitter16_1_out_7), .out_8(splitter16_1_out_8),
    .out_9(splitter16_1_out_9), .out_10(splitter16_1_out_10), .out_11(splitter16_1_out_11),
    .out_12(splitter16_1_out_12), .out_13(splitter16_1_out_13), .out_14(splitter16_1_out_14),
    .out_15(splitter16_1_out_15), .out_16(splitter16_1_out_16), .out_17(splitter16_1_out_17),
    .out_2(splitter16_1_out_2));
  not not_1 (not_1_out, in_2);
  and and_1 (and_1_out, splitter16_1_out_2, not_1_out);
  and and_2 (and_2_out, splitter16_1_out_3, not_1_out);
  and and_3 (and_3_out, splitter16_1_out_4, not_1_out);
  and and_4 (and_4_out, splitter16_1_out_5, not_1_out);
  and and_5 (and_5_out, splitter16_1_out_6, not_1_out);
  and and_6 (and_6_out, splitter16_1_out_7, not_1_out);
  and and_7 (and_7_out, splitter16_1_out_8, not_1_out);
  and and_8 (and_8_out, splitter16_1_out_9, not_1_out);
  and and_9 (and_9_out, splitter16_1_out_10, not_1_out);
  and and_10 (and_10_out, splitter16_1_out_11, not_1_out);
  and and_11 (and_11_out, splitter16_1_out_12, not_1_out);
  and and_12 (and_12_out, splitter16_1_out_13, not_1_out);
  and and_13 (and_13_out, splitter16_1_out_14, not_1_out);
  and and_14 (and_14_out, splitter16_1_out_15, not_1_out);
  and and_15 (and_15_out, splitter16_1_out_16, not_1_out);
  and and_16 (and_16_out, splitter16_1_out_17, not_1_out);
  and and_17 (and_17_out, in_2, splitter16_1_out_2);
  and and_18 (and_18_out, in_2, splitter16_1_out_3);
  and and_19 (and_19_out, in_2, splitter16_1_out_4);
  and and_20 (and_20_out, in_2, splitter16_1_out_5);
  and and_21 (and_21_out, in_2, splitter16_1_out_6);
  and and_22 (and_22_out, in_2, splitter16_1_out_7);
  and and_23 (and_23_out, in_2, splitter16_1_out_8);
  and and_24 (and_24_out, in_2, splitter16_1_out_9);
  and and_25 (and_25_out, in_2, splitter16_1_out_10);
  and and_26 (and_26_out, in_2, splitter16_1_out_11);
  and and_27 (and_27_out, in_2, splitter16_1_out_12);
  and and_28 (and_28_out, in_2, splitter16_1_out_13);
  and and_29 (and_29_out, in_2, splitter16_1_out_14);
  and and_30 (and_30_out, in_2, splitter16_1_out_15);
  and and_31 (and_31_out, in_2, splitter16_1_out_16);
  and and_32 (and_32_out, in_2, splitter16_1_out_17);
  Merger16 merger16_1 (
    .in_2(and_2_out), .in_3(and_3_out), .in_4(and_4_out), .in_5(and_5_out), .in_6(and_6_out),
    .in_7(and_7_out), .in_8(and_8_out), .in_9(and_9_out), .in_10(and_10_out), .in_11(and_11_out),
    .in_1(and_1_out), .in_12(and_12_out), .in_13(and_13_out), .in_14(and_14_out), .in_15(and_15_out),
    .in_16(and_16_out), .out_17(out_3));
  Merger16 merger16_2 (
    .in_2(and_18_out), .in_3(and_19_out), .in_4(and_20_out), .in_5(and_21_out), .in_6(and_22_out),
    .in_7(and_23_out), .in_8(and_24_out), .in_9(and_25_out), .in_10(and_26_out), .in_11(and_27_out),
    .in_1(and_17_out), .in_12(and_28_out), .in_13(and_29_out), .in_14(and_30_out), .in_15(and_31_out),
    .in_16(and_32_out), .out_17(out_4));
endmodule

module DMUX4WAY16 (
  input  [15:0] in_1,
  input  [1:0] in_2,
  output [15:0] out_3,
  output [15:0] out_4,
  output [15:0] out_5,
  output [15:0] out_6
);

  wire splitter2_1_out_2, splitter2_1_out_3;
  wire [15:0] dmux16_1_out_3, dmux16_1_out_4;

  DMUX16 dmux16_1 (.in_2(splitter2_1_out_3), .in_1(in_1), .out_3(dmux16_1_out_3), .out_4(dmux16_1_out_4));
  SPLITTER2 splitter2_1 (.in_1(in_2), .out_3(splitter2_1_out_3), .out_2(splitter2_1_out_2));
  DMUX16 dmux16_2 (.in_2(splitter2_1_out_2), .in_1(dmux16_1_out_3), .out_3(out_3), .out_4(out_4));
  DMUX16 dmux16_3 (.in_2(splitter2_1_out_2), .in_1(dmux16_1_out_4), .out_3(out_5), .out_4(out_6));
endmodule

module DMUX8WAY (
  input  in_1,
  input  [2:0] in_2,
  output out_3,
  output out_4,
  output out_5,
  output out_6,
  output out_7,
  output out_8,
  output out_9,
  output out_10
);

  wire cdmux_1_out_3, cdmux_1_out_4, cdmux_2_out_3, cdmux_2_out_4, cdmux_3_out_3, cdmux_3_out_4,
       splitter3_1_out_2, splitter3_1_out_3, splitter3_1_out_4;

  CDMUX cdmux_1 (.in_2(splitter3_1_out_4), .in_1(in_1), .out_3(cdmux_1_out_3), .out_4(cdmux_1_out_4));
  SPLITTER3 splitter3_1 (.in_1(in_2), .out_3(splitter3_1_out_3), .out_4(splitter3_1_out_4), .out_2(splitter3_1_out_2));
  CDMUX cdmux_2 (.in_2(splitter3_1_out_3), .in_1(cdmux_1_out_3), .out_3(cdmux_2_out_3), .out_4(cdmux_2_out_4));
  CDMUX cdmux_3 (.in_2(splitter3_1_out_3), .in_1(cdmux_1_out_4), .out_3(cdmux_3_out_3), .out_4(cdmux_3_out_4));
  CDMUX cdmux_4 (.in_2(splitter3_1_out_2), .in_1(cdmux_2_out_3), .out_3(out_3), .out_4(out_4));
  CDMUX cdmux_5 (.in_2(splitter3_1_out_2), .in_1(cdmux_2_out_4), .out_3(out_5), .out_4(out_6));
  CDMUX cdmux_6 (.in_2(splitter3_1_out_2), .in_1(cdmux_3_out_3), .out_3(out_7), .out_4(out_8));
  CDMUX cdmux_7 (.in_2(splitter3_1_out_2), .in_1(cdmux_3_out_4), .out_3(out_9), .out_4(out_10));
endmodule

module SPLITTER3 (
  input  [2:0] in_1,
  output out_2,
  output out_3,
  output out_4
);

  BitSelector #(.width(3)) bitselector_1 (.in(in_1), .out(out_2), .sel(2'b00));
  BitSelector #(.width(3)) bitselector_2 (.in(in_1), .out(out_3), .sel(2'b01));
  BitSelector #(.width(3)) bitselector_3 (.in(in_1), .out(out_4), .sel(2'b10));
endmodule

module DMUX4WAY (
  input  in_1,
  input  [1:0] in_2,
  output out_3,
  output out_4,
  output out_5,
  output out_6
);

  wire cdmux_1_out_3, cdmux_1_out_4, splitter2_1_out_2, splitter2_1_out_3;

  CDMUX cdmux_1 (.in_2(splitter2_1_out_3), .in_1(in_1), .out_3(cdmux_1_out_3), .out_4(cdmux_1_out_4));
  SPLITTER2 splitter2_1 (.in_1(in_2), .out_3(splitter2_1_out_3), .out_2(splitter2_1_out_2));
  CDMUX cdmux_2 (.in_2(splitter2_1_out_2), .in_1(cdmux_1_out_3), .out_3(out_3), .out_4(out_4));
  CDMUX cdmux_3 (.in_2(splitter2_1_out_2), .in_1(cdmux_1_out_4), .out_3(out_5), .out_4(out_6));
endmodule

module HALFADDER (
  input  in_1,
  input  in_2,
  output out_3,
  output out_4
);

  xor xor_1 (out_3, in_1, in_2);
  and and_1 (out_4, in_1, in_2);
endmodule

module FULLADDER (
  input  in_1,
  input  in_2,
  input  in_3,
  output out_4,
  output out_5
);

  wire and_1_out, and_2_out, xor_1_out;

  xor xor_1 (xor_1_out, in_1, in_2);
  and and_1 (and_1_out, in_1, in_2);
  xor xor_2 (out_4, xor_1_out, in_3);
  and and_2 (and_2_out, xor_1_out, in_3);
  xor xor_3 (out_5, and_2_out, and_1_out);
endmodule

module CADDER (
  input  [15:0] in_1,
  input  [15:0] in_2,
  output [15:0] out_3,
  output out_4
);

  wire fulladder_1_out_5, fulladder_2_out_5, fulladder_3_out_5, fulladder_4_out_5, fulladder_5_out_5,
       fulladder_6_out_5, fulladder_7_out_5, fulladder_8_out_5, fulladder_9_out_5, fulladder_10_out_5,
       fulladder_11_out_5, fulladder_12_out_5, fulladder_13_out_5, fulladder_14_out_5, halfadder_1_out_4;

  HALFADDER halfadder_1 (.in_1(in_1[0]), .in_2(in_2[0]), .out_4(halfadder_1_out_4), .out_3(out_3[0]));
  FULLADDER fulladder_1 (
    .in_3(in_2[1]), .in_1(halfadder_1_out_4), .in_2(in_1[1]), .out_4(out_3[1]), .out_5(fulladder_1_out_5));
  FULLADDER fulladder_2 (
    .in_3(in_2[2]), .in_1(fulladder_1_out_5), .in_2(in_1[2]), .out_4(out_3[2]), .out_5(fulladder_2_out_5));
  FULLADDER fulladder_3 (
    .in_3(in_2[3]), .in_1(fulladder_2_out_5), .in_2(in_1[3]), .out_4(out_3[3]), .out_5(fulladder_3_out_5));
  FULLADDER fulladder_4 (
    .in_3(in_2[4]), .in_1(fulladder_3_out_5), .in_2(in_1[4]), .out_4(out_3[4]), .out_5(fulladder_4_out_5));
  FULLADDER fulladder_5 (
    .in_3(in_2[5]), .in_1(fulladder_4_out_5), .in_2(in_1[5]), .out_4(out_3[5]), .out_5(fulladder_5_out_5));
  FULLADDER fulladder_6 (
    .in_3(in_2[6]), .in_1(fulladder_5_out_5), .in_2(in_1[6]), .out_4(out_3[6]), .out_5(fulladder_6_out_5));
  FULLADDER fulladder_7 (
    .in_3(in_2[7]), .in_1(fulladder_6_out_5), .in_2(in_1[7]), .out_4(out_3[7]), .out_5(fulladder_7_out_5));
  FULLADDER fulladder_8 (
    .in_3(in_2[8]), .in_1(fulladder_7_out_5), .in_2(in_1[8]), .out_4(out_3[8]), .out_5(fulladder_8_out_5));
  FULLADDER fulladder_9 (
    .in_3(in_2[9]), .in_1(fulladder_8_out_5), .in_2(in_1[9]), .out_4(out_3[9]), .out_5(fulladder_9_out_5));
  FULLADDER fulladder_10 (
    .in_3(in_2[10]), .in_1(fulladder_9_out_5), .in_2(in_1[10]), .out_4(out_3[10]), .out_5(fulladder_10_out_5));
  FULLADDER fulladder_11 (
    .in_3(in_2[11]), .in_1(fulladder_10_out_5), .in_2(in_1[11]), .out_4(out_3[11]), .out_5(fulladder_11_out_5));
  FULLADDER fulladder_12 (
    .in_3(in_2[12]), .in_1(fulladder_11_out_5), .in_2(in_1[12]), .out_4(out_3[12]), .out_5(fulladder_12_out_5));
  FULLADDER fulladder_13 (
    .in_3(in_2[13]), .in_1(fulladder_12_out_5), .in_2(in_1[13]), .out_4(out_3[13]), .out_5(fulladder_13_out_5));
  FULLADDER fulladder_14 (
    .in_3(in_2[14]), .in_1(fulladder_13_out_5), .in_2(in_1[14]), .out_4(out_3[14]), .out_5(fulladder_14_out_5));
  FULLADDER fulladder_15 (
    .in_3(in_2[15]), .in_1(fulladder_14_out_5), .in_2(in_1[15]), .out_4(out_3[15]), .out_5(out_4));
endmodule

module ALU (
  input  [15:0] x,
  input  zx,
  input  nx,
  input  [15:0] y,
  input  zy,
  input  ny,
  input  f,
  input  no,
  output ng,
  output zr,
  output [15:0] ruedi
);

  wire [15:0] adder_1_out, and_1_out, demultiplexer_1_out0, demultiplexer_2_out0, multiplexer_1_out,
       multiplexer_2_out, multiplexer_3_out, not_1_out, not_2_out, not_3_out;

  Demultiplexer #(.width(16)) demultiplexer_1 (.out0(demultiplexer_1_out0), .in(x), .sel(zx));  // open: out1
  Demultiplexer #(.width(16)) demultiplexer_2 (.out0(demultiplexer_2_out0), .in(y), .sel(zy));  // open: out1
  Multiplexer #(.width(16)) multiplexer_1 (
    .in0(demultiplexer_1_out0), .in1(not_1_out), .out(multiplexer_1_out), .sel(nx));
  assign not_1_out = ~demultiplexer_1_out0;  // NOT_Gate not_1, 16 bits wide
  Multiplexer #(.width(16)) multiplexer_2 (
    .in0(demultiplexer_2_out0), .in1(not_2_out), .out(multiplexer_2_out), .sel(ny));
  assign not_2_out = ~demultiplexer_2_out0;  // NOT_Gate not_2, 16 bits wide
  assign and_1_out = multiplexer_1_out & multiplexer_2_out;  // AND_Gate and_1, 16 bits wide
  Adder #(.width(16)) adder_1 (.a(multiplexer_1_out), .b(multiplexer_2_out), .out(adder_1_out));  // open: cin, cout
  Multiplexer #(.width(16)) multiplexer_3 (.in0(and_1_out), .in1(adder_1_out), .out(multiplexer_3_out), .sel(f));
  assign not_3_out = ~multiplexer_3_out;  // NOT_Gate not_3, 16 bits wide
  Multiplexer #(.width(16)) multiplexer_4 (.in0(multiplexer_3_out), .in1(not_3_out), .out(ruedi), .sel(no));
  Comparator #(.width(16)) comparator_1 (.a({16{1'b0}}), .b(ruedi), .gt(ng), .eq(zr));  // open: lt
endmodule

module INC16 (
  input  [15:0] in_1,
  output [15:0] out_2
);

  Adder #(.width(16)) adder_1 (.a(in_1), .b(16'h1), .out(out_2));  // open: cin, cout
endmodule

module CLA (
  input  c,
  input  [15:0] a,
  input  [15:0] b,
  output [15:0] res,
  output cout
);

  wire and_1_out, and_2_out, and_3_out, and_4_out, and_5_out, and_6_out, and_7_out, and_8_out, and_9_out,
       and_10_out, and_11_out, and_12_out, and_13_out, and_14_out, and_15_out, and_16_out, and_17_out,
       and_18_out, and_19_out, and_20_out, and_21_out, and_22_out, and_23_out, and_24_out, and_25_out,
       and_26_out, and_27_out, and_28_out, and_29_out, and_30_out, and_31_out, and_32_out, or_1_out,
       or_2_out, or_3_out, or_4_out, or_5_out, or_6_out, or_7_out, or_8_out, or_9_out, or_10_out, or_11_out,
       or_12_out, or_13_out, or_14_out, or_15_out, xor_1_out, xor_2_out, xor_3_out, xor_4_out, xor_5_out,
       xor_6_out, xor_7_out, xor_8_out, xor_9_out, xor_10_out, xor_11_out, xor_12_out, xor_13_out,
       xor_14_out, xor_15_out, xor_16_out;

  and and_1 (and_1_out, b[0], a[0]);
  and and_2 (and_2_out, b[1], a[1]);
  and and_3 (and_3_out, b[2], a[2]);
  and and_4 (and_4_out, b[3], a[3]);
  and and_5 (and_5_out, b[4], a[4]);
  and and_6 (and_6_out, b[5], a[5]);
  and and_7 (and_7_out, b[6], a[6]);
  and and_8 (and_8_out, b[7], a[7]);
  and and_9 (and_9_out, b[8], a[8]);
  and and_10 (and_10_out, b[9], a[9]);
  and and_11 (and_11_out, b[10], a[10]);
  and and_12 (and_12_out, b[11], a[11]);
  and and_13 (and_13_out, b[12], a[12]);
  and and_14 (and_14_out, b[13], a[13]);
  and and_15 (and_15_out, b[14], a[14]);
  and and_16 (and_16_out, b[15], a[15]);
  xor xor_1 (xor_1_out, a[0], b[0]);
  and and_17 (and_17_out, c, xor_1_out);
  xor xor_2 (xor_2_out, a[1], b[1]);
  xor xor_3 (xor_3_out, a[2], b[2]);
  xor xor_4 (xor_4_out, a[3], b[3]);
  xor xor_5 (xor_5_out, a[4], b[4]);
  xor xor_6 (xor_6_out, a[5], b[5]);
  xor xor_7 (xor_7_out, a[6], b[6]);
  xor xor_8 (xor_8_out, a[7], b[7]);
  xor xor_9 (xor_9_out, a[8], b[8]);
  xor xor_10 (xor_10_out, a[9], b[9]);
  xor xor_11 (xor_11_out, a[10], b[10]);
  xor xor_12 (xor_12_out, a[11], b[11]);
  xor xor_13 (xor_13_out, a[12], b[12]);
  xor xor_14 (xor_14_out, a[13], b[13]);
  xor xor_15 (xor_15_out, a[14], b[14]);
  xor xor_16 (xor_16_out, a[15], b[15]);
  or or_1 (or_1_out, and_17_out, and_1_out);
  and and_18 (and_18_out, or_1_out, xor_2_out);
  or or_2 (or_2_out, and_18_out, and_2_out);
  and and_19 (and_19_out, or_2_out, xor_3_out);
  or or_3 (or_3_out, and_19_out, and_3_out);
  and and_20 (and_20_out, or_3_out, xor_4_out);
  or or_4 (or_4_out, and_20_out, and_4_out);
  and and_21 (and_21_out, or_4_out, xor_5_out);
  or or_5 (or_5_out, and_21_out, and_5_out);
  and and_22 (and_22_out, or_5_out, xor_6_out);
  or or_6 (or_6_out, and_22_out, and_6_out);
  and and_23 (and_23_out, or_6_out, xor_7_out);
  or or_7 (or_7_out, and_23_out, and_7_out);
  and and_24 (and_24_out, or_7_out, xor_8_out);
  or or_8 (or_8_out, and_24_out, and_8_out);
  and and_25 (and_25_out, or_8_out, xor_9_out);
  or or_9 (or_9_out, and_25_out, and_9_out);
  and and_26 (and_26_out, or_9_out, xor_10_out);
  or or_10 (or_10_out, and_26_out, and_10_out);
  and and_27 (and_27_out, or_10_out, xor_11_out);
  or or_11 (or_11_out, and_27_out, and_11_out);
  and and_28 (and_28_out, or_11_out, xor_12_out);
  or or_12 (or_12_out, and_28_out, and_12_out);
  and and_29 (and_29_out, or_12_out, xor_13_out);
  or or_13 (or_13_out, and_29_out, and_13_out);
  and and_30 (and_30_out, or_13_out, xor_14_out);
  or or_14 (or_14_out, and_30_out, and_14_out);
  and and_31 (and_31_out, or_14_out, xor_15_out);
  or or_15 (or_15_out, and_31_out, and_15_out);
  and and_32 (and_32_out, or_15_out, xor_16_out);
  or or_16 (cout, and_32_out, and_16_out);
  xor xor_17 (res[0], c, xor_1_out);
  xor xor_18 (res[1], or_1_out, xor_2_out);
  xor xor_19 (res[2], or_2_out, xor_3_out);
  xor xor_20 (res[3], or_3_out, xor_4_out);
  xor xor_21 (res[4], or_4_out, xor_5_out);
  xor xor_22 (res[5], or_5_out, xor_6_out);
  xor xor_23 (res[6], or_6_out, xor_7_out);
  xor xor_24 (res[7], or_7_out, xor_8_out);
  xor xor_25 (res[8], or_8_out, xor_9_out);
  xor xor_26 (res[9], or_9_out, xor_10_out);
  xor xor_27 (res[10], or_10_out, xor_11_out);
  xor xor_28 (res[11], or_11_out, xor_12_out);
  xor xor_29 (res[12], or_12_out, xor_13_out);
  xor xor_30 (res[13], or_13_out, xor_14_out);
  xor xor_31 (res[14], or_14_out, xor_15_out);
  xor xor_32 (res[15], or_15_out, xor_16_out);
endmodule

module BIT (
  input  in_1,
  input  in_2,
  input  in_3,
  output out_4
);

  wire multiplexer_1_out;

  Multiplexer multiplexer_1 (.in0(out_4), .in1(in_1), .out(multiplexer_1_out), .sel(in_2));
  D_Flip_Flop d_ff_1 (.D(multiplexer_1_out), .clk(in_3), .Q(out_4));  // open: Qn, preset, reset
endmodule

module REG16 (
  input  [15:0] INPUT16,
  input  SEL,
  input  SAVE,
  output [15:0] out_4
);

  wire undriven, undriven_2, undriven_3, undriven_4, undriven_5, undriven_6, undriven_7, undriven_8,
       undriven_9, undriven_10, undriven_11, undriven_12, undriven_13, undriven_14, undriven_15;
  wire [15:0] multiplexer_1_out;

  Multiplexer #(.width(16)) multiplexer_1 (.in0(out_4), .in1(INPUT16), .out(multiplexer_1_out), .sel(SEL));
  D_Flip_Flop d_ff_1 (.D(multiplexer_1_out[0]), .clk(SAVE), .Q(out_4[0]), .reset(undriven));  // open: Qn, preset
  D_Flip_Flop d_ff_2 (
    .D(multiplexer_1_out[1]), .clk(SAVE), .Q(out_4[1]), .preset(undriven), .reset(undriven_2));  // open: Qn
  D_Flip_Flop d_ff_3 (
    .D(multiplexer_1_out[2]), .clk(SAVE), .Q(out_4[2]), .preset(undriven_2), .reset(undriven_3));  // open: Qn
  D_Flip_Flop d_ff_4 (
    .D(multiplexer_1_out[3]), .clk(SAVE), .Q(out_4[3]), .preset(undriven_3), .reset(undriven_4));  // open: Qn
  D_Flip_Flop d_ff_5 (
    .D(multiplexer_1_out[4]), .clk(SAVE), .Q(out_4[4]), .preset(undriven_4), .reset(undriven_5));  // open: Qn
  D_Flip_Flop d_ff_6 (
    .D(multiplexer_1_out[5]), .clk(SAVE), .Q(out_4[5]), .preset(undriven_5), .reset(undriven_6));  // open: Qn
  D_Flip_Flop d_ff_7 (
    .D(multiplexer_1_out[6]), .clk(SAVE), .Q(out_4[6]), .preset(undriven_6), .reset(undriven_7));  // open: Qn
  D_Flip_Flop d_ff_8 (
    .D(multiplexer_1_out[7]), .clk(SAVE), .Q(out_4[7]), .preset(undriven_7), .reset(undriven_8));  // open: Qn
  D_Flip_Flop d_ff_9 (
    .D(multiplexer_1_out[8]), .clk(SAVE), .Q(out_4[8]), .preset(undriven_8), .reset(undriven_9));  // open: Qn
  D_Flip_Flop d_ff_10 (
    .D(multiplexer_1_out[9]), .clk(SAVE), .Q(out_4[9]), .preset(undriven_9), .reset(undriven_10));  // open: Qn
  D_Flip_Flop d_ff_11 (
    .D(multiplexer_1_out[10]), .clk(SAVE), .Q(out_4[10]), .preset(undriven_10), .reset(undriven_11));  // open: Qn
  D_Flip_Flop d_ff_12 (
    .D(multiplexer_1_out[11]), .clk(SAVE), .Q(out_4[11]), .preset(undriven_11), .reset(undriven_12));  // open: Qn
  D_Flip_Flop d_ff_13 (
    .D(multiplexer_1_out[12]), .clk(SAVE), .Q(out_4[12]), .preset(undriven_12), .reset(undriven_13));  // open: Qn
  D_Flip_Flop d_ff_14 (
    .D(multiplexer_1_out[13]), .clk(SAVE), .Q(out_4[13]), .preset(undriven_13), .reset(undriven_14));  // open: Qn
  D_Flip_Flop d_ff_15 (
    .D(multiplexer_1_out[14]), .clk(SAVE), .Q(out_4[14]), .preset(undriven_14), .reset(undriven_15));  // open: Qn
  D_Flip_Flop d_ff_16 (.D(multiplexer_1_out[15]), .clk(SAVE), .Q(out_4[15]), .preset(undriven_15));  // open: Qn, reset
endmodule

module RAM16 (
  input  [15:0] in_1,
  input  [1:0] in_2,
  input  in_3,
  input  in_4,
  output [15:0] out_5
);

  wire [15:0] demultiplexer_1_out0, demultiplexer_1_out1, demultiplexer_1_out2, demultiplexer_1_out3,
       reg16_1_out_4, reg16_2_out_4, reg16_3_out_4, reg16_4_out_4;

  Demultiplexer #(.select(2), .width(16)) demultiplexer_1 (
    .out0(demultiplexer_1_out0), .out1(demultiplexer_1_out1), .out2(demultiplexer_1_out2),
    .out3(demultiplexer_1_out3), .in(in_1), .sel(in_2));
  REG16 reg16_1 (.SEL(in_3), .SAVE(in_4), .INPUT16(demultiplexer_1_out0), .out_4(reg16_1_out_4));
  REG16 reg16_2 (.SEL(in_3), .SAVE(in_4), .INPUT16(demultiplexer_1_out1), .out_4(reg16_2_out_4));
  Multiplexer #(.select(2), .width(16)) multiplexer_1 (
    .in0(reg16_1_out_4), .in1(reg16_2_out_4), .in2(reg16_3_out_4), .in3(reg16_4_out_4), .out(out_5),
    .sel(in_2));
  REG16 reg16_3 (.SEL(in_3), .SAVE(in_4), .INPUT16(demultiplexer_1_out2), .out_4(reg16_3_out_4));
  REG16 reg16_4 (.SEL(in_3), .SAVE(in_4), .INPUT16(demultiplexer_1_out3), .out_4(reg16_4_out_4));
endmodule

module COUNT16 (
  input  [15:0] IN16,
  input  in_2,
  input  INC,
  input  LOAD,
  input  RESET,
  output [15:0] out_6
);

  wire or_1_out;
  wire [15:0] adder_1_out, multiplexer_1_out, multiplexer_2_out, multiplexer_3_out;

  Multiplexer #(.width(16)) multiplexer_1 (.in1(adder_1_out), .out(multiplexer_1_out), .sel(INC));  // open: in0
  Adder #(.width(16)) adder_1 (.a(out_6), .b(16'h1), .out(adder_1_out));  // open: cin, cout
  Multiplexer #(.width(16)) multiplexer_2 (.in0(multiplexer_1_out), .in1(IN16), .out(multiplexer_2_out), .sel(LOAD));
  Multiplexer #(.width(16)) multiplexer_3 (
    .in0(multiplexer_2_out), .in1({16{1'b0}}), .out(multiplexer_3_out), .sel(RESET));
  REG16 reg16_1 (.SEL(or_1_out), .SAVE(in_2), .INPUT16(multiplexer_3_out), .out_4(out_6));
  or or_1 (or_1_out, INC, LOAD, RESET);
endmodule

module CPU (
  input  [15:0] INSTRUCTION,
  input  [15:0] MEMORY,
  input  RESET,
  input  TAKT
);

  wire [15:0] alu_1_ruedi, count16_1_out_6, multiplexer_1_out, multiplexer_2_out, reg16_1_out_4,
       reg16_2_out_4;

  Multiplexer #(.width(16)) multiplexer_1 (.in0(alu_1_ruedi), .in1(INSTRUCTION), .out(multiplexer_1_out));  // open: sel
  REG16 reg16_1 (.INPUT16(multiplexer_1_out), .out_4(reg16_1_out_4));  // open: SEL, SAVE
  REG16 reg16_2 (.INPUT16(alu_1_ruedi), .out_4(reg16_2_out_4));  // open: SEL, SAVE
  Multiplexer #(.width(16)) multiplexer_2 (.in0(reg16_1_out_4), .in1(MEMORY), .out(multiplexer_2_out));  // open: sel
  COUNT16 count16_1 (.IN16(reg16_1_out_4), .RESET(RESET), .in_2(TAKT), .out_6(count16_1_out_6));  // open: INC, LOAD
  ALU alu_1 (.y(multiplexer_2_out), .x(reg16_2_out_4), .ruedi(alu_1_ruedi));  // open: zx, nx, zy, ny, f, no, ng, zr
endmodule
